// Digital circuit Contador verilog.dig as structural Verilog
module Contador_verilog (
  input  B3,
  input  B2,
  input  B1,
  input  B0,
  output S3,
  output S2,
  output S1,
  output S0
);

  Seven_Seg_Hex seven_seg_hex_1 (.d({B3, B2, B1, B0}), .dp(1'b0));

  // Other names for the same wires on the sheet: S4 = S0
endmodule

/* Test case Padrão 7421:
B3 B2 B1 B0  S3 S2 S1 S0
0 0 0 0 	0 0 0 0
0 0 0 1 	0 0 0 1
0 0 1 0 	0 0 1 0
0 0 1 1 	0 0 1 1
0 1 0 0 	0 1 0 0
0 1 0 1 	0 1 0 1
0 1 1 0 	0 1 1 0 
0 1 1 1 	1 0 0 0
1 0 0 0 	1 0 0 1
1 0 0 1 	1 0 1 0 
*/
