// Digital circuit Documento de Christian.dig as structural Verilog
module Documento_de_Christian (
  input  B3,
  input  B2,
  input  B1,
  input  B0,
  output b,
  output c,
  output d,
  output e,
  output a,
  output f,
  output g
);

  Seven_Seg_Hex seven_seg_hex_1 (.d({B3, B2, B1, B0}), .dp(1'b0));
  bcd_to_7seg #(.applicationType("IVERILOG")) u_bcd_to_7seg (
    .B3(B3), .B2(B2), .B1(B1), .B0(B0), .a(a), .b(b), .c(c), .d(d), .e(e), .f(f), .g(g));
  Seven_Seg seven_seg_1 (.a(a), .b(b), .c(c), .d(d), .e(e), .f(f), .g(g), .dp(1'b0));
endmodule

/* Test case 7SEG:
B3 B2 B1 B0     a b c d e f g
0 0 0 0 	1 1 1 1 1 1 0
0 0 0 1 	0 1 1 0 0 0 0
0 0 1 0 	1 1 0 1 1 0 1
0 0 1 1 	1 1 1 1 0 0 1
0 1 0 0 	0 1 1 0 0 1 1
0 1 0 1 	1 0 1 1 0 1 1
0 1 1 0 	1 0 1 1 1 1 1
0 1 1 1 	1 1 1 0 0 0 0
1 0 0 0 	1 1 1 1 1 1 1 
1 0 0 1 	1 1 1 1 0 1 1
*/

/* Code of bcd_to_7seg:
module bcd_to_7seg(
    input B3, B2, B1, B0,
    output reg a,
    output reg b,
    output reg c,
    output reg d,
    output reg e,
    output reg f,
    output reg g
);

always @(B3 or B2 or B1 or B0) begin
    case ({B3, B2, B1, B0})
        4'b0000: {a,b,c,d,e,f,g} = 7'b1111110; // 0
        4'b0001: {a,b,c,d,e,f,g} = 7'b0110000; // 1
        4'b0010: {a,b,c,d,e,f,g} = 7'b1101101; // 2
        4'b0011: {a,b,c,d,e,f,g} = 7'b1111001; // 3
        4'b0100: {a,b,c,d,e,f,g} = 7'b0110011; // 4
        4'b0101: {a,b,c,d,e,f,g} = 7'b1011011; // 5
        4'b0110: {a,b,c,d,e,f,g} = 7'b1011111; // 6
        4'b0111: {a,b,c,d,e,f,g} = 7'b1110000; // 7
        4'b1000: {a,b,c,d,e,f,g} = 7'b1111111; // 8
        4'b1001: {a,b,c,d,e,f,g} = 7'b1111011; // 9
        default: {a,b,c,d,e,f,g} = 7'b0000000; 
    endcase
end

endmodule
*/
