// Digital circuit Template  Questão 12.dig as structural Verilog
module \Template__Questão_12  (
  input  A,
  input  B,
  input  S,
  output Y
);

  Multiplexer multiplexer_1 (.sel(S), .in_0(A), .in_1(B), .out(Y));
endmodule

/* Test case Mux2x1:
A B S Y 
0 0 0 0 	
0 0 1 0 	
0 1 0 0 	
0 1 1 1 	
1 0 0 1 	
1 0 1 0 	
1 1 0 1 	
1 1 1 1 	
*/
