// Digital circuit Template  Questão 3 (1).dig as structural Verilog
module \Template__Questão_3__1  (
  input  B3,
  input  B2,
  input  B1,
  input  B0,
  output S4,
  output S3,
  output S2,
  output S1
);

  wire and_1_out, and_2_out, and_3_out, and_4_out, and_5_out, and_6_out, not_1_out, not_2_out, not_3_out;

  Seven_Seg_Hex seven_seg_hex_1 (.d({S1, S2, S3, B0}), .dp(1'b0));
  not not_1 (not_1_out, B0);
  and and_1 (and_1_out, B2, B0);
  and and_2 (and_2_out, B2, B1);
  and and_3 (and_3_out, B2, B1);
  and and_4 (and_4_out, B2, not_1_out);
  and and_5 (and_5_out, B1, not_2_out);
  not not_2 (not_2_out, B2);
  not not_3 (not_3_out, B1);
  and and_6 (and_6_out, B2, not_3_out, B0);
  or or_1 (S1, B3, and_1_out, and_2_out);
  or or_2 (S2, B3, and_3_out, and_4_out);
  or or_3 (S3, B3, and_5_out, and_6_out);

  assign S4 = B0;
endmodule

/* Test case Padrão 2421:
B3 B2 B1 B0  S3 S2 S1 S0
0 0 0 0 	0 0 0 0
0 0 0 1 	0 0 0 1
0 0 1 0 	0 0 1 0
0 0 1 1 	0 0 1 1
0 1 0 0 	0 1 0 0
0 1 0 1 	1 0 1 1
0 1 1 0 	1 1 0 0
0 1 1 1 	1 1 0 1
1 0 0 0 	1 1 1 0
1 0 0 1 	1 1 1 1
*/
