// Digital circuit Template  Questão 8.dig as structural Verilog
module \Template__Questão_8  (
  input  B3,
  input  B2,
  input  B1,
  input  B0,
  output S3,
  output S2,
  output S1,
  output S0,
  output S4
);

  Seven_Seg_Hex seven_seg_hex_1 (.d({B3, B2, B1, B0}), .dp(1'b0));
endmodule

/* Test case Padrao 2 de 5:
B3 B2 B1 B0  S4 S3 S2 S1 S0
0 0 0 0 	0 0 0 1 1
0 0 0 1 	0 0 1 0 1
0 0 1 0 	0 0 1 1 0
0 0 1 1 	0 1 0 0 1
0 1 0 0 	0 1 0 1 0
0 1 0 1 	0 1 1 0 0
0 1 1 0 	1 0 0 0 1 
0 1 1 1 	1 0 0 1 0
1 0 0 0 	1 0 1 0 0
1 0 0 1 	1 1 0 0 0
*/
