// Digital circuit Template Contador Assíncrono Mod11.dig as structural Verilog
module \Template_Contador_Assíncrono_Mod11  (
  input  Clk,
  output Q3,
  output Q2,
  output Q1,
  output Q0
);

  wire d_ff_1_nq, d_ff_2_nq, d_ff_3_nq, d_ff_4_nq;

  Seven_Seg_Hex seven_seg_hex_1 (.d({Q3, Q2, Q1, Q0}), .dp(1'b0));
  D_FF d_ff_1 (.D(d_ff_1_nq), .C(Clk), .Q(Q0), .nQ(d_ff_1_nq));
  D_FF d_ff_2 (.D(d_ff_2_nq), .C(d_ff_1_nq), .Q(Q1), .nQ(d_ff_2_nq));
  D_FF d_ff_3 (.D(d_ff_3_nq), .C(d_ff_2_nq), .Q(Q2), .nQ(d_ff_3_nq));
  D_FF d_ff_4 (.D(d_ff_4_nq), .C(d_ff_3_nq), .Q(Q3), .nQ(d_ff_4_nq));
endmodule

/* Test case CntMod11:
Clk Rst Q3 Q2 Q1 Q0
0 0 bits(4,0) 
repeat(8) C 1 bits(4,n+1)
c 0 bits(4,0)
repeat(10) C 1 bits(4,n+1)
c 1 bits(4,0)
repeat(10) C 1 bits(4,n+1)
c 1 bits(4,0)
*/
