// Digital circuit Template Contador Mod8 u1 d3.dig as structural Verilog
module Template_Contador_Mod8_u1_d3 (
  input  U,
  input  Clk,
  output Q0,
  output Q1,
  output Q2
);

  wire and_1_out, and_2_out, and_3_out, nQ0, nQ1, nQ2, nU, or_1_out;

  Seven_Seg_Hex seven_seg_hex_1 (.d({1'b0, Q2, Q1, Q0}), .dp(1'b0));
  not not_1 (nU, U);
  T_FF t_ff_1 (.T(or_1_out), .C(Clk), .Q(Q2), .nQ(nQ2));
  or or_1 (or_1_out, and_3_out, and_2_out, and_1_out);
  and and_1 (and_1_out, nQ1, nU);
  and and_2 (and_2_out, nQ0, Q1, nU);
  and and_3 (and_3_out, Q0, Q1, U);
  T_FF t_ff_2 (.T(Q0), .C(Clk), .Q(Q1), .nQ(nQ1));
  T_FF t_ff_3 (.T(1'b1), .C(Clk), .Q(Q0), .nQ(nQ0));

  // Notes on the sheet:
  //   U: default 1
endmodule

/* Test case MOD8 U1 D3:
#MOD8 u1 d3
Clk U Q2 Q1 Q0
C 1 bits(3,1)
C 1 bits(3,2)
C 1 bits(3,3)
C 1 bits(3,4)
C 1 bits(3,5)
C 1 bits(3,6)
C 1 bits(3,7)
C 1 bits(3,0)
C 0 bits(3,5)
C 0 bits(3,2)
C 0 bits(3,7)
C 0 bits(3,4)
C 0 bits(3,1)
C 0 bits(3,6)
C 0 bits(3,3)
C 0 bits(3,0)
*/
