// Digital circuit Template Conversão de circuito 2.dig as structural Verilog
module \Template_Conversão_de_circuito_2  (
  input  B,
  input  C,
  input  A,
  output X
);

  wire nand_1_out, nand_2_out, nand_3_out, nand_4_out, nand_5_out, nand_6_out, nand_7_out, nand_8_out,
       nand_9_out, nand_10_out;

  nand nand_1 (nand_1_out, A, A);
  nand nand_2 (nand_2_out, C, C);
  nand nand_3 (nand_3_out, A, C, B);
  nand nand_4 (nand_4_out, nand_1_out, nand_2_out);
  nand nand_5 (nand_5_out, nand_3_out, nand_3_out);
  nand nand_6 (nand_6_out, B, B);
  nand nand_7 (nand_7_out, A, nand_4_out, nand_6_out);
  nand nand_8 (nand_8_out, nand_7_out, nand_7_out);
  nand nand_9 (nand_9_out, nand_8_out, nand_8_out);
  nand nand_10 (nand_10_out, nand_5_out, nand_5_out);
  nand nand_11 (X, nand_9_out, nand_10_out);
endmodule

/* Test case CONVERSÃO CIRCUITO 2:
A B C X 
0 0 0 0
0 0 1 0
0 1 0 0
0 1 1 0
1 0 0 1 
1 0 1 1
1 1 0 0
1 1 1 1
*/
