// Digital circuit Template FFJK.dig as structural Verilog
module Template_FFJK (
  input  j,
  input  Clk,
  input  rst,
  input  set,
  input  k,
  output Q,
  output nQ
);

  FFJK #(.applicationType("IVERILOG")) u_FFJK (.set(set), .Clk(Clk), .j(j), .k(k), .rst(rst), .Q(Q), .nQ(nQ));
endmodule

/* Test case FFJK:
Clk rst set j k Q nQ
c   0    1  x x 0 1
c   1    0  x x 1 0
c   1    1  1 1 0 1
c   1    1  1 1 1 0
c   0    1  x x 0 1
c   1    0  x x 1 0
*/

/* Code of FFJK:
module FFJK(input set,  Clk,  j,   k,   rst, output reg Q,  nQ);
  always @(posedge Clk, negedge rst) begin
    if(rst==0) begin  
      Q <= 1'b0;
      nQ <= 1'b1;
    end else if(set ==1) begin 
      Q <= 1'b1;
      nQ <= 1'b0;
    end else if(j==1 && k==0) begin 
      Q <= 1'b1;
      nQ <= 1'b0;
    end else if(j==0 && k==1) begin
      Q <= 1'b0;
      nQ <= 1'b1;
    end else if(j==1 && k==1) begin 
      Q <= ~Q;
      nQ <= ~nQ;
    end;
  end;
endmodule
*/
