// Digital circuit Template Questão 5.dig as structural Verilog
module \Template_Questão_5  (
  input  B3,
  input  B2,
  input  B1,
  input  B0,
  output S3,
  output S2,
  output S1,
  output S0
);

  Seven_Seg_Hex seven_seg_hex_1 (.d({B3, B2, B1, B0}), .dp(1'b0));
  conversor7421 #(.applicationType("IVERILOG")) u_conversor7421 (
    .B0(B0), .B1(B1), .B2(B2), .B3(B3), .S0(S0), .S1(S1), .S2(S2), .S3(S3));
endmodule

/* Test case Padrão 7421:
B3 B2 B1 B0  S3 S2 S1 S0
0 0 0 0 	0 0 0 0
0 0 0 1 	0 0 0 1
0 0 1 0 	0 0 1 0
0 0 1 1 	0 0 1 1
0 1 0 0 	0 1 0 0
0 1 0 1 	0 1 0 1
0 1 1 0 	0 1 1 0 
0 1 1 1 	1 0 0 0
1 0 0 0 	1 0 0 1
1 0 0 1 	1 0 1 0 
*/

/* Code of conversor7421:
module conversor7421(input B0,B1,B2,B3, output reg S0,S1,S2,S3);
	always @(*) begin
		if((B3==1 && B2==0) || (B2==1 && B1==1 && B0==1)) begin
			S3 = 1;
		end else if((B2==1 && B0==0) || (B2==1 && B1==0 && B0==1)) begin
			S2 = 1;
		end else if((B3==1 && B0==1) || (B2==0 && B1==1) || (B1==1 && B0==0)) begin
			S1 = 1;
		end else if((B3==0 && B2==0 && B0==1) || (B3==0 && B1==0 && B0==1) || (B3==1 && B0==0)) begin
			S0 = 1;
		end
	end
endmodule
*/
