// Digital circuit aquelaquestao.dig as structural Verilog
module aquelaquestao (
  input  X1,
  input  X0,
  input  Y1,
  input  Y0,
  output Z3,
  output Z2,
  output Z1,
  output Z0
);

  Seven_Seg_Hex seven_seg_hex_1 (.d({2'b00, X1, X0}), .dp(1'b0));
  Seven_Seg_Hex seven_seg_hex_2 (.d({2'b00, Y1, Y0}), .dp(1'b0));
  Seven_Seg_Hex seven_seg_hex_3 (.d({Z3, Z2, Z1, Z0}), .dp(1'b0));
endmodule

/* Test case Multiplicador:
X1 X0 Y1 Y0 Z3 Z2 Z1 Z0
loop(a,4)
  loop(b,4)
      bits(2,a) bits(2,b)  bits(4,a*b)
  end loop
end loop
*/
