// Digital circuit automato_0110.dig as structural Verilog
module automato_0110 (
  input  Clk,
  output Q0,
  output Q1,
  output Hit,
  output d,
  output HitReference
);

  wire and_1_out, and_2_out, and_3_out, nd, or_1_out, or_2_out, Rst;

  Seven_Seg_Hex seven_seg_hex_1 (.d({2'b00, Q1, Q0}), .dp(1'b0));
  T_FF t_ff_1 (.T(or_1_out), .C(Clk), .Q(Q1));  // open: nQ
  or or_1 (or_1_out, and_2_out, and_1_out);
  and and_1 (and_1_out, nd, Q1);
  and and_2 (and_2_out, Q0, d);
  stimulus #(.applicationType("IVERILOG")) u_stimulus (
    .clk(Clk), .rst(Rst), .dado(24'h653060), .\ref (4'b0110), .intc(1'b0), .rep(1'b1), .ds(d),
    .hit(HitReference));  // open: comparacao
  T_FF t_ff_2 (.T(or_2_out), .C(Clk), .Q(Q0));  // open: nQ
  not not_1 (nd, d);
  or or_2 (or_2_out, and_3_out, Q1);
  and and_3 (and_3_out, Q0, d);
  and and_4 (Hit, Q1, nd, Q0);
  Reset u_Rst (.out(Rst));
endmodule

/* Code of stimulus:
module stimulus (input clk, rst, input [23:0] dado, input [3:0] ref, input intc, rep, output reg ds, output hit, output reg [3:0] comparacao);
  reg [23:0] dadoTrabalho; 
  reg [6:0] cntBits; 
  
  
  reg enHit; 
  always @ (negedge rst or posedge clk) begin
    if (rst==0)begin
      ds <= dado[23];
      dadoTrabalho <= dado; 
      comparacao <= 0;
      enHit <= 1; 
      cntBits <=0; 
    end
    else begin
           cntBits <= cntBits+1;		
           ds <= dadoTrabalho[23];
           dadoTrabalho <= {dadoTrabalho[22:0],1'b0}; 
           comparacao[0] <= dadoTrabalho[23]; 
           
      	   if (hit) 
             if (rep==0)
               enHit <= 0;  
             else if (intc==0) begin
                     comparacao[4:1] <= 4'd0; 
                     cntBits <= 0;  
                   end 
                   else begin
                     comparacao[4:1] <= comparacao[3:0]; 
                   end
            else comparacao[4:1] <= comparacao[3:0];
         

         end
   end

   assign hit = ( (enHit) && (comparacao == ref) && (cntBits>=3)? 1 : 0 ); //
endmodule
*/

/* Test case:
Clk Hit HitReference d Q1 Q0
repeat(24) c X X X X X
*/
