// Digital circuit automato_1100CR.dig as structural Verilog
module automato_1100CR (
  input  Clk,
  output Q0,
  output Q1,
  output Hit,
  output d,
  output HitReference
);

  wire nd, Rst;

  Seven_Seg_Hex seven_seg_hex_1 (.d({2'b00, Q1, Q0}), .dp(1'b0));
  stimulus #(.applicationType("IVERILOG")) u_stimulus (
    .clk(Clk), .rst(Rst), .dado(24'hc46468), .\ref (4'b1100), .intc(1'b0), .rep(1'b1), .ds(d),
    .hit(HitReference));  // open: comparacao
  automato #(.applicationType("IVERILOG")) u_automato (.clk(Clk), .rst(Rst), .d(d), .hit(Hit), .estado({Q1, Q0}));
  not not_1 (nd, d);
  Reset u_Rst (.out(Rst));
endmodule

/* Code of stimulus:
module stimulus (input clk, rst, input [23:0] dado, input [3:0] ref, input intc, rep, output reg ds, output hit, output reg [3:0] comparacao);
  reg [23:0] dadoTrabalho; 
  reg [6:0] cntBits; 
  
  
  reg enHit; 
  always @ (negedge rst or posedge clk) begin
    if (rst==0)begin
      ds <= dado[23];
      dadoTrabalho <= dado; 
      comparacao <= 0;
      enHit <= 1; 
      cntBits <=0; 
    end
    else begin
           cntBits <= cntBits+1;		
           ds <= dadoTrabalho[23];
           dadoTrabalho <= {dadoTrabalho[22:0],1'b0}; 
           comparacao[0] <= dadoTrabalho[23]; 
           
      	   if (hit) 
             if (rep==0)
               enHit <= 0;  
             else if (intc==0) begin
                     comparacao[4:1] <= 4'd0; 
                     cntBits <= 0;  
                   end 
                   else begin
                     comparacao[4:1] <= comparacao[3:0]; 
                   end
            else comparacao[4:1] <= comparacao[3:0];
         

         end
   end

   assign hit = ( (enHit) && (comparacao == ref) && (cntBits>=3)? 1 : 0 ); //
endmodule
*/

/* Code of automato:
module automato(input clk, rst, d, output hit, output reg [1:0] estado);

	always@(posedge clk or negedge rst)
	   begin
		if(rst==0)
		   estado <= 0;
		else
		  case(estado)
			0: estado <= (d==1? 1:0);
			1: estado <= (d==1? 2:0);
			2: estado <= (d==0? 3:2);
			3: estado <= (d==0? 0:1);
		  endcase
	   end
	assign hit = (estado==3 && d==0? 1:0);
endmodule
*/

/* Test case:
Clk Hit HitReference d Q1 Q0
repeat(24) c X X X X X
*/
