// Digital circuit verilog checa se par.dig as structural Verilog
module verilog_checa_se_par (
  input  B0,
  input  B1,
  input  B2,
  output Y
);

  even_detector #(.applicationType("IVERILOG")) u_even_detector (.B0(B0), .B1(B1), .B2(B2), .Y(Y));
endmodule

/* Test case:
B2 B1 B0 Y 
0 0 0 1 	
0 0 1 0 	
0 1 0 1 	
0 1 1 0 	
1 0 0 1 	
1 0 1 0 	
1 1 0 1 	
1 1 1 0 	
*/

/* Code of even_detector:
module even_detector( input B0,B1,B2, output reg Y);
  always @(*) begin
    if (B0 == 0) begin
	Y = 1;
    end else begin
      Y <= 0;//É par
    end
  end
endmodule
*/
